# Fritzing sketch aresfrit (saved by Fritzing 0.9.3b)
breadboards: 1

parts:
  Mega = Arduino Mega 2560 (Rev3)
  H_Bridge = Monster Moto Shield
  U1 = LIPO-2000mAh [package=lipo-2000]

nets:
  N1: Mega.A0, H_Bridge.EN1_-_A0
  N2: Mega.A1, H_Bridge.EN2_-_A1
  N3: Mega.A2, H_Bridge.CS1_-_A2
  N4: Mega.A3, H_Bridge.CS2_-_A3
  N5: Mega.A4, H_Bridge.A4
  N6: Mega.A5, H_Bridge.A5
  N7: Mega.AREF, H_Bridge.AREF
  N8: Mega.GND, H_Bridge.GND_-_GND@0, H_Bridge.GND_-_GND@1, H_Bridge.GND_-_GND@2, U1.-
  N9: Mega.D13_PWM, H_Bridge.D13
  N10: Mega.D12_PWM, H_Bridge.D12
  N11: Mega.D11_PWM, H_Bridge.D11
  N12: Mega.D10_PWM, H_Bridge.D10
  N13: Mega.D9_PWM, H_Bridge.INB2_-_D9
  N14: Mega.D8_PWM, H_Bridge.INB1_-_D8
  N15: Mega.RESET, H_Bridge.RES
  3V3: Mega.3V3, H_Bridge.3.3V
  5V: Mega.5V, H_Bridge.5V
  VIN: Mega.VIN, H_Bridge.VIN, U1.+
  N16: Mega.D0_RX0, H_Bridge.RX
  N17: Mega.D1_TX0, H_Bridge.TX
  N18: Mega.D2_PWM, H_Bridge.D2
  N19: Mega.D3_PWM, H_Bridge.D3
  N20: Mega.D4_PWM, H_Bridge.INA2_-_D4
  N21: Mega.D5_PWM, H_Bridge.PWM1_-_D5
  N22: Mega.D6_PWM, H_Bridge.PWM2_-_D6
  N23: Mega.D7_PWM, H_Bridge.INA1_-_D7
